// Logisim project Conrol_Unit.circ as structural Verilog: 8 circuits, main circuit Control_Unit
module Control_Unit (
  input  [6:0] Func_7,
  input  [2:0] Func_3,
  input  [6:0] OpCode,
  output out_4,
  output out_5,
  output out_6,
  output out_7,
  output [1:0] out_8,
  output out_9,
  output [1:0] out_10,
  output [1:0] out_11,
  output [4:0] ALU_Code
);

  wire type_decode_1_auipc, type_decode_1_branches, type_decode_1_i_type, type_decode_1_jal,
       type_decode_1_jalr, type_decode_1_loads, type_decode_1_lui, type_decode_1_r_type, type_decode_1_stores;
  wire [2:0] control_decode_1_alu_op;

  Type_Decode type_decode_1 (
    .in_1(OpCode), .I_Type(type_decode_1_i_type), .Loads(type_decode_1_loads), .JALR(type_decode_1_jalr),
    .Stores(type_decode_1_stores), .Branches(type_decode_1_branches), .LUI(type_decode_1_lui),
    .AUIPC(type_decode_1_auipc), .JAL(type_decode_1_jal), .R_Type(type_decode_1_r_type));
  Control_Decode control_decode_1 (
    .R_Type(type_decode_1_r_type), .I_Type(type_decode_1_i_type), .Loads(type_decode_1_loads),
    .JALR(type_decode_1_jalr), .Stores(type_decode_1_stores), .Branches(type_decode_1_branches),
    .LUI(type_decode_1_lui), .AUIPC(type_decode_1_auipc), .JAL(type_decode_1_jal), .RegWrite(out_4),
    .MemWrite(out_5), .MemRead(out_6), .Branch(out_7), .Op_A(out_8), .Op_B(out_9), .Next_PC(out_10),
    .ALU_Op(control_decode_1_alu_op), .Imm_Sel(out_11));
  ALU_Control alu_control_1 (
    .ALUOP2(control_decode_1_alu_op[2]), .ALUOP1(control_decode_1_alu_op[1]),
    .ALUOP0(control_decode_1_alu_op[0]), .Func7(Func_7[5]), .Func32(Func_3[2]), .Func31(Func_3[1]),
    .Func30(Func_3[0]), .ALUControl4(ALU_Code[4]), .ALUControl3(ALU_Code[3]), .ALUControl2(ALU_Code[2]),
    .ALUControl1(ALU_Code[1]), .ALUControl0(ALU_Code[0]));
endmodule

module Type_Decode (
  input  [6:0] in_1,
  output R_Type,
  output I_Type,
  output Loads,
  output JALR,
  output Stores,
  output Branches,
  output LUI,
  output AUIPC,
  output JAL
);

  // Probe on in_1
  Comparator #(.width(7)) comparator_1 (.a(in_1), .b(7'b0110011), .eq(R_Type));  // open: gt, lt
  Comparator #(.width(7)) comparator_2 (.a(in_1), .b(7'b0010011), .eq(I_Type));  // open: gt, lt
  Comparator #(.width(7)) comparator_3 (.a(in_1), .b(7'b0000011), .eq(Loads));  // open: gt, lt
  Comparator #(.width(7)) comparator_4 (.a(in_1), .b(7'b1100111), .eq(JALR));  // open: gt, lt
  Comparator #(.width(7)) comparator_5 (.a(in_1), .b(7'b0100011), .eq(Stores));  // open: gt, lt
  Comparator #(.width(7)) comparator_6 (.a(in_1), .b(7'b1100011), .eq(Branches));  // open: gt, lt
  Comparator #(.width(7)) comparator_7 (.a(in_1), .b(7'b0110111), .eq(LUI));  // open: gt, lt
  Comparator #(.width(7)) comparator_8 (.a(in_1), .b(7'b0010111), .eq(AUIPC));  // open: gt, lt
  Comparator #(.width(7)) comparator_9 (.a(in_1), .b(7'b1101111), .eq(JAL));  // open: gt, lt
endmodule

module Control_Decode (
  input  R_Type,
  input  I_Type,
  input  Loads,
  input  JALR,
  input  Stores,
  input  Branches,
  input  LUI,
  input  AUIPC,
  input  JAL,
  output RegWrite,
  output MemWrite,
  output MemRead,
  output Branch,
  output [1:0] Op_A,
  output Op_B,
  output [1:0] Next_PC,
  output [2:0] ALU_Op,
  output [1:0] Imm_Sel
);

  or or_1 (RegWrite, R_Type, I_Type, Loads, JALR, LUI, AUIPC, JAL);
  Op_A_Sel op_a_sel_1 (.JALR(JALR), .AUIPC(AUIPC), .JAL(JAL), .out_4(Op_A));
  or or_2 (Op_B, I_Type, Loads, Stores, LUI, JAL);
  Next_PC_Sel next_pc_sel_1 (.JALR(JALR), .B_Type(Branches), .JAL(JAL), .out_4(Next_PC));
  ALU_Operation alu_operation_1 (
    .R_Type(R_Type), .I_Type(I_Type), .Loads(Loads), .JALR(JALR), .Stores(Stores), .Branches(Branches),
    .LUI(LUI), .AUIPC(AUIPC), .JAL(JAL), .out_10(ALU_Op));
  Extend_Sel extend_sel_1 (.I(I_Type), .LB(Loads), .SB(Stores), .LUI(LUI), .AUIPC(AUIPC), .out_6(Imm_Sel));

  assign Branch = Branches;
  assign MemRead = Loads;
  assign MemWrite = Stores;
endmodule

module Op_A_Sel (
  input  JALR,
  input  AUIPC,
  input  JAL,
  output [1:0] out_4
);

  or or_1 (out_4[1], JALR, JAL);

  assign out_4[0] = AUIPC;
endmodule

module Next_PC_Sel (
  input  JALR,
  input  B_Type,
  input  JAL,
  output [1:0] out_4
);

  or or_1 (out_4[1], JALR, B_Type);
  or or_2 (out_4[0], JALR, JAL);
endmodule

module Extend_Sel (
  input  I,
  input  LB,
  input  SB,
  input  LUI,
  input  AUIPC,
  output [1:0] out_6
);

  wire and_1_out, and_2_out, and_3_out, and_4_out, and_5_out, and_6_out, not_1_out, not_2_out, not_3_out,
       not_4_out;

  not not_1 (not_1_out, I);
  not not_2 (not_2_out, LB);
  not not_3 (not_3_out, LUI);
  not not_4 (not_4_out, AUIPC);
  and and_1 (and_1_out, I, not_3_out, not_4_out);
  and and_2 (and_2_out, SB, not_3_out, not_4_out);
  or or_1 (out_6[1], and_1_out, and_2_out, and_3_out);
  and and_3 (and_3_out, LB, not_3_out, not_4_out);
  and and_4 (and_4_out, not_1_out, not_2_out, AUIPC);
  and and_5 (and_5_out, not_1_out, not_2_out, LUI);
  or or_2 (out_6[0], and_4_out, and_5_out, and_6_out);
  and and_6 (and_6_out, not_1_out, not_2_out, SB);
endmodule

module ALU_Control (
  input  ALUOP2,
  input  ALUOP1,
  input  ALUOP0,
  input  Func7,
  input  Func32,
  input  Func31,
  input  Func30,
  output ALUControl4,
  output ALUControl3,
  output ALUControl2,
  output ALUControl1,
  output ALUControl0
);

  wire and_1_out, and_2_out, and_3_out, and_4_out, and_5_out, and_6_out, and_7_out, and_8_out, and_9_out,
       and_10_out, and_11_out, and_12_out, not_1_out, not_2_out, not_3_out;

  not not_1 (not_1_out, ALUOP2);
  not not_2 (not_2_out, ALUOP1);
  not not_3 (not_3_out, ALUOP0);
  and and_1 (and_1_out, not_1_out, ALUOP1, ALUOP0);
  and and_2 (and_2_out, ALUOP2, not_2_out, ALUOP0);
  and and_3 (and_3_out, not_1_out, not_2_out, Func7);
  and and_4 (and_4_out, ALUOP2, ALUOP1);
  and and_5 (and_5_out, ALUOP1, ALUOP0);
  and and_6 (and_6_out, not_1_out, ALUOP1, ALUOP0);
  and and_7 (and_7_out, not_2_out, Func32);
  and and_8 (and_8_out, ALUOP1, ALUOP0);
  and and_9 (and_9_out, not_2_out, Func31);
  and and_10 (and_10_out, not_2_out, Func30);
  and and_11 (and_11_out, ALUOP2, ALUOP1, not_3_out);
  and and_12 (and_12_out, not_1_out, ALUOP1, ALUOP0);
  or or_1 (ALUControl4, and_1_out, and_2_out);
  or or_2 (ALUControl3, and_3_out, and_4_out, and_5_out);
  or or_3 (ALUControl2, and_6_out, and_7_out);
  or or_4 (ALUControl1, and_8_out, and_9_out);
  or or_5 (ALUControl0, and_10_out, and_11_out, and_12_out);
endmodule

module ALU_Operation (
  input  R_Type,
  input  I_Type,
  input  Loads,
  input  JALR,
  input  Stores,
  input  Branches,
  input  LUI,
  input  AUIPC,
  input  JAL,
  output [2:0] out_10
);

  wire nand_1_out, or_1_out;
  wire [2:0] priority_encoder_1_out;

  or or_1 (or_1_out, JALR, JAL);
  Priority_Encoder priority_encoder_1 (
    .in0(R_Type), .in1(I_Type), .in2(Loads), .in3(or_1_out), .in4(Stores), .in5(Branches), .in6(LUI),
    .in7(AUIPC), .out(priority_encoder_1_out), .en_in(1'b1));  // open: gs, en_out
  nand nand_1 (nand_1_out, R_Type, I_Type, Loads, JALR, Stores, Branches, LUI, AUIPC, JAL);
  Multiplexer #(.width(3)) multiplexer_1 (.in0(priority_encoder_1_out), .in1(3'b000), .out(out_10), .sel(nand_1_out));
endmodule
