// Logisim project Immediate_Generation.circ as structural Verilog: 1 circuit, main circuit Immediate_Generator
module Immediate_Generator (
  input  [31:0] in_1,
  input  [31:0] in_2,
  output [31:0] S_Immediate,
  output [31:0] B_Immediate,
  output [31:0] U_Immediate,
  output [31:0] J_Type,
  output [31:0] I_Immediate
);

  wire [31:0] bit_extender_1_out, bit_extender_3_out, bit_extender_4_out;

  assign bit_extender_1_out = {{12{in_1[31]}}, in_1[31:12]};  // Bit_Extender bit_extender_1
  assign S_Immediate = {{20{in_1[31]}}, {in_1[31:25], in_1[11:7]}};  // Bit_Extender bit_extender_2
  assign bit_extender_3_out = {{19{in_1[31]}}, {in_1[31], in_1[7], in_1[30:25], in_1[11:8], 1'b0}};  // Bit_Extender bit_extender_3
  Shifter #(.width(32)) shifter_1 (.in(bit_extender_1_out), .\dist (5'b01100), .out(U_Immediate));
  assign bit_extender_4_out = {{11{in_1[31]}}, {in_1[31], in_1[19:12], in_1[20], in_1[30:21], 1'b0}};  // Bit_Extender bit_extender_4
  assign I_Immediate = {{20{in_1[31]}}, in_1[31:20]};  // Bit_Extender bit_extender_5
  Adder #(.width(32)) adder_1 (.a(bit_extender_3_out), .b(in_2), .out(B_Immediate));  // open: cin, cout
  Adder #(.width(32)) adder_2 (.a(in_2), .b(bit_extender_4_out), .out(J_Type));  // open: cin, cout
endmodule
