// Logisim project RV32I.circ as structural Verilog: 2 circuits, main circuit RV_32I
module RV_32I (
  input  CLK,
  input  RST
);

  wire and_2_out, arithmetic_logic_unit_1_out_5, control_unit_1_out_4, control_unit_1_out_5,
       control_unit_1_out_6, control_unit_1_out_7, control_unit_1_out_9;
  wire [1:0] control_unit_1_out_8, control_unit_1_out_10, control_unit_1_out_11;
  wire [4:0] control_unit_1_alu_code;
  wire [9:0] arithmetic_logic_unit_1_out_4;
  wire [31:0] adder_1_out, adder_2_out, and_1_out, Data_Memery_dout, immediate_generator_1_b_immediate,
       immediate_generator_1_i_immediate, immediate_generator_1_j_type, immediate_generator_1_s_immediate,
       immediate_generator_1_u_immediate, Instruction_Memory_dout, multiplexer_1_out, multiplexer_2_out,
       multiplexer_3_out, multiplexer_4_out, multiplexer_5_out, multiplexer_6_out, PC_q,
       register_file_32_1_readdata1, register_file_32_1_readdata2;
  wire [31:10] arithmetic_logic_unit_1_out_4_2;

  Multiplexer #(.select(2), .width(32)) multiplexer_1 (
    .in0(adder_1_out), .in1(immediate_generator_1_j_type), .in2(multiplexer_2_out), .in3(and_1_out),
    .out(multiplexer_1_out), .sel(control_unit_1_out_10));
  Multiplexer #(.width(32)) multiplexer_2 (
    .in0(adder_1_out), .in1(immediate_generator_1_b_immediate), .out(multiplexer_2_out), .sel(and_2_out));
  Register #(.width(32)) PC (.D(multiplexer_1_out), .Q(PC_q), .clk(CLK), .clr(RST));  // open: en
  Adder #(.width(32)) adder_1 (.a(32'h4), .b(PC_q), .out(adder_1_out));  // open: cin, cout
  RAM #(.addrWidth(10), .dataWidth(32), .enables("line"), .\type ("nonvolatile")) Instruction_Memory (
    .addr(PC_q[9:0]), .clk(CLK), .dout(Instruction_Memory_dout));  // open: we, din
  Multiplexer #(.width(32)) multiplexer_3 (
    .in0({arithmetic_logic_unit_1_out_4_2, arithmetic_logic_unit_1_out_4}), .in1(Data_Memery_dout),
    .out(multiplexer_3_out), .sel(control_unit_1_out_6));
  assign and_1_out = 32'hfffffffe & adder_2_out;  // AND_Gate and_1, 32 bits wide
  Immediate_Generator immediate_generator_1 (
    .in_2(PC_q), .in_1(Instruction_Memory_dout), .B_Immediate(immediate_generator_1_b_immediate),
    .U_Immediate(immediate_generator_1_u_immediate), .J_Type(immediate_generator_1_j_type),
    .I_Immediate(immediate_generator_1_i_immediate), .S_Immediate(immediate_generator_1_s_immediate));
  Control_Unit control_unit_1 (
    .OpCode(Instruction_Memory_dout[6:0]), .Func_7(Instruction_Memory_dout[31:25]),
    .Func_3(Instruction_Memory_dout[14:12]), .out_4(control_unit_1_out_4), .out_5(control_unit_1_out_5),
    .out_6(control_unit_1_out_6), .out_7(control_unit_1_out_7), .out_8(control_unit_1_out_8),
    .out_9(control_unit_1_out_9), .out_10(control_unit_1_out_10), .out_11(control_unit_1_out_11),
    .ALU_Code(control_unit_1_alu_code));
  Register_File_32 register_file_32_1 (
    .ReadReg(control_unit_1_out_4), .Write_Reg_94da2a91(Instruction_Memory_dout[11:7]),
    .WriteData(multiplexer_3_out), .CLK(CLK), .RST(RST), .ReadReg1(Instruction_Memory_dout[19:15]),
    .ReadReg2(Instruction_Memory_dout[24:20]), .ReadData1(register_file_32_1_readdata1),
    .ReadData2(register_file_32_1_readdata2));
  Adder #(.width(32)) adder_2 (
    .a(register_file_32_1_readdata1), .b(immediate_generator_1_i_immediate), .out(adder_2_out));  // open: cin, cout
  Multiplexer #(.select(2), .width(32)) multiplexer_4 (
    .in0({32{1'b0}}), .in1(immediate_generator_1_u_immediate), .in2(immediate_generator_1_i_immediate),
    .in3(immediate_generator_1_s_immediate), .out(multiplexer_4_out), .sel(control_unit_1_out_11));
  Multiplexer #(.select(2), .width(32)) multiplexer_5 (
    .in0(register_file_32_1_readdata1), .in1(adder_1_out), .in2(PC_q), .out(multiplexer_5_out),
    .sel(control_unit_1_out_8));  // open: in3
  Multiplexer #(.width(32)) multiplexer_6 (
    .in0(register_file_32_1_readdata2), .in1(multiplexer_4_out), .out(multiplexer_6_out),
    .sel(control_unit_1_out_9));
  Arithmetic_Logic_Unit arithmetic_logic_unit_1 (
    .A(multiplexer_5_out), .B(multiplexer_6_out), .ALU_Control(control_unit_1_alu_code),
    .out_4({arithmetic_logic_unit_1_out_4_2, arithmetic_logic_unit_1_out_4}),
    .out_5(arithmetic_logic_unit_1_out_5));
  RAM #(.addrWidth(10), .dataWidth(32), .\type ("nonvolatile")) Data_Memery (
    .addr(arithmetic_logic_unit_1_out_4), .we(control_unit_1_out_5), .oe(control_unit_1_out_6), .clk(CLK),
    .din(register_file_32_1_readdata2), .dout(Data_Memery_dout));
  and and_2 (and_2_out, arithmetic_logic_unit_1_out_5, control_unit_1_out_7);
endmodule

module Testing (
);

  wire [1:0] undriven;
  wire [31:0] adder_1_out, multiplexer_1_out, multiplexer_2_out, PC_q, ram_1_dout,
       register_file_32_1_readdata1;

  Multiplexer #(.select(2), .width(32)) multiplexer_1 (
    .in0(adder_1_out), .out(multiplexer_1_out), .sel(undriven));  // open: in1, in2, in3
  Register #(.width(32)) PC (.D(multiplexer_1_out), .Q(PC_q));  // open: en, clk, clr
  Adder #(.width(32)) adder_1 (.a(32'h4), .b(PC_q), .out(adder_1_out));  // open: cin, cout
  RAM #(.addrWidth(24), .dataWidth(32)) ram_1 (.addr(PC_q[23:0]), .dout(ram_1_dout));  // open: we, oe, clk, din
  Immediate_Generator immediate_generator_1 (
    .in_2(PC_q), .in_1(ram_1_dout));  // open: B_Immediate, U_Immediate, J_Type, I_Immediate, S_Immediate
  Register_File_32 register_file_32_1 (.ReadData1(register_file_32_1_readdata1));  // open: ReadReg, Write_Reg_94da2a91, WriteData, CLK, RST, ReadReg1, ReadReg2, ReadData2
  Multiplexer #(.select(2), .width(32)) multiplexer_2 (
    .in0(register_file_32_1_readdata1), .out(multiplexer_2_out));  // open: in1, in2, in3, sel
  Arithmetic_Logic_Unit arithmetic_logic_unit_1 (.A(multiplexer_2_out));  // open: B, ALU_Control, out_4, out_5
  RAM #(.addrWidth(24), .dataWidth(32)) ram_2 ();  // open: addr, we, oe, clk, din, dout

  // Notes on the sheet:
  //   NEXT PC
endmodule
